# Fritzing sketch esquema do projeto (saved by Fritzing 0.9.2b)
breadboards: 1

parts:
  Part1 = Arduino Uno (Rev3)
  R1 = Resistor [tolerance=±5% resistance=1k package=THT]
  R2 = Resistor [tolerance=±5% resistance=1k package=THT]
  R3 = Resistor [tolerance=±5% resistance=1k package=THT]
  R4 = Resistor [tolerance=±5% resistance=1k package=THT]
  S1 = Pushbutton [package="[THT]"]
  S2 = Pushbutton [package="[THT]"]
  LED1 = LED - 5mm [color="Red (633nm)" package="5 mm [THT]"]
  LED2 = LED - 5mm [color="Green (570nm)" package="5 mm [THT]"]
  Part2 = SRF05 Ultrasonic Rangefinder
  J1 = Piezo Speaker
  R5 = Resistor [tolerance=±5% resistance=220 package=THT]

nets:
  N1: Part1.D9_PWM, LED2.anode
  N2: Part1.D10_PWM/SS, LED1.anode
  N3: Part1.D11_PWM/MOSI, Part2.Trig
  N4: Part1.D12/MISO, Part2.Echo
  GND: Part1.GND, R1.Pin_0, R2.Pin_0, R3.Pin_0, R4.Pin_0, Part2.GND, R5.Pin_1
  5V: Part1.D2, Part1.D3_PWM, Part1.5V, S1.Pin_3, S1.Pin_4, S2.Pin_3, S2.Pin_4, Part2.VCC
  N5: Part1.D6_PWM, J1.pin2
  N6: R1.Pin_1, LED2.cathode
  N7: R2.Pin_1, LED1.cathode
  N8: R3.Pin_1, S2.Pin_1, S2.Pin_2
  N9: R4.Pin_1, S1.Pin_1, S1.Pin_2
  N10: J1.pin1, R5.Pin_0

// code stored in the sketch: ProjetoMic2_v13.ino

#include <NewPing.h>
#include <avr/interrupt.h>
#include "pitches.h"

const byte TONE_PIN = 6;
//const byte DIST_PIN = A0;
const byte ECHO_PIN = 12;  // Arduino pin tied to echo pin on the ultrasonic sensor.
const byte TRIGGER_PIN = 11;  // Arduino pin tied to trigger pin on the ultrasonic sensor.
const byte LED_PISCA = 10;
const byte LED_ON  = 9;
const unsigned int CLK_TIMER = 15625;
const float MIN_FREQ = 1;
const float MAX_FREQ = 5000;
int max_distance = 20; // Maximum distance we want to ping for (in centimeters). Maximum sensor distance is rated at 400-500cm.
byte on = LOW;
unsigned int top = 0;
void sing();
void configInt0();
void configInt1();
void configTimer1();
void configpersonal();
void buzz(int targetPin, long frequency, long len);

void setup() {
  PRR = 0; // Sair do modo de baixo consumo
  UBRR0 = 103;
  UCSR0A = 0;
  UCSR0B = (1 << TXEN0) | (1 << RXEN0); // Int TX desabilitada, circuito TX habilitado
  UCSR0C = (1 << UCSZ01) | (1 << UCSZ00); // 8 bits, sem paridade
  pinMode(LED_ON, OUTPUT);
  pinMode(LED_PISCA, OUTPUT);
  pinMode(TONE_PIN, OUTPUT);
  sei();
  configInt0();
  configInt1();
  configTimer1();
  configpersonal();
}

void loop() {
  NewPing sonar(TRIGGER_PIN, ECHO_PIN, max_distance); // NewPing setup of pins and maximum distance.
  digitalWrite(LED_ON, on);
  delay(50);
  if (on) {
    EIMSK &= (0xFF ^ (1 << INT1)); // desabilita a interrup��o 1
    unsigned int dist = sonar.ping_cm();
//    unsigned int dist = analogRead(DIST_PIN)*max_distance/1023;
    if (dist != 0) {
      TIMSK1 = (1 << OCIE1A);
      top = CLK_TIMER/(-6.49213*log(0.0428622*dist));
      //top = CLK_TIMER*(1/MAX_FREQ) + (CLK_TIMER*(1/MIN_FREQ - 1/MAX_FREQ)*dist)/max_distance;
      if (top > 65535){
        top = 65535;
      }
      //OCR1A = top ;
    }
    else {
      TIMSK1 = (0 << OCIE1A); // desliga o timer com o buzzer
    }
    
    Serial.print("Ping: ");
    Serial.print(dist);
    Serial.println("cm");
    Serial.println(top);
  }
  else{
    EIMSK |= (1 << INT1);
  }
}

//------------------------------------------------------------------------------------------------------//

void configInt0() {
  EICRA = (1 << ISC01) | (1 << ISC00); // Registrador de configura��o do modo RISING
  EIMSK = (1 << INT0); // M�scara de habilita��o individual de interrup��es externas
}
void configInt1() {
  EICRA |= (1 << ISC11) | (1 << ISC10); // Registrador de configura��o do modo RISING
  EIMSK |= (1 << INT1); // M�scara de habilita��o individual de interrup��es externas
}

void configTimer1() {
  TCCR1A = 0; // Limpa TCCR1A
  TCCR1B = (1 << CS12) | (1 << CS10) | (1 << WGM12); // Prescaler divide por 64 f_clk = 16 MHz/256 = 250 kHz
                                                     // Modo CTC (Clear Timer on Compare)
  TIMSK1 = (0 << OCIE1A); // desabilita interrup��o comparacao timer 1
  OCR1A = top;
}

ISR(INT0_vect) { //Tratador da INT0
  if(on){
    Serial.println("Desligando...");
  }
  else{
    Serial.println("Bem-vindo ao seu assistente de conducao!");
    sing();
  }
  on = !on;
}

ISR(INT1_vect) { //Tratador da INT1
  while(!( UCSR0A & (1<<UDRE0) ) );
  Serial.println("Configuracoes do sistema");
  configpersonal();
}

ISR(TIMER1_COMPA_vect) { // Timer interrupt vector.
  TCCR1B = (0 << CS12) | (0 << CS11) | (0 << CS10);
  buzz(TONE_PIN, NOTE_C5, 100);
  OCR1A = top ;
  TCCR1B = (1 << CS12) | (1 << CS10) | (1 << WGM12);
}

void configpersonal() {
  Serial.println("Escolha o nivel de instrucao do condutor do veiculo: ");
  Serial.println("1.   Iniciante ");
  Serial.println("2.   Intermediario ");
  Serial.println("3.   Profissional ");
  while (!( UCSR0A & (1 << RXC0) ) ); //espera ate que o usuario digite algo
  char ctrlUser = UDR0; //atribui o que foi digitado a ctrlUser
  switch (ctrlUser) {
    case '1':
      max_distance = 20;
      break;
    case '2':
      max_distance = 30;
      break;
    case '3':
      max_distance = 40;
      break;
  }
  Serial.println(ctrlUser);
  Serial.print("distancia maxima: ");
  Serial.println(max_distance);
}

void buzz(int targetPin, long frequency, long len) {
  digitalWrite(LED_PISCA,HIGH);
  long delayValue = 1000000/frequency/2; // calculate the delay value between transitions
  //// 1 second's worth of microseconds, divided by the frequency, then split in half since
  //// there are two phases to each cycle
  long numCycles = frequency * len/ 1000; // calculate the number of cycles for proper timing
  //// multiply frequency, which is really cycles per second, by the number of seconds to 
  //// get the total number of cycles to produce
  for (long i=0; i < numCycles; i++){ // for the calculated length of time...
    digitalWrite(targetPin,HIGH); // write the buzzer pin high to push out the diaphram
    delayMicroseconds(delayValue); // wait for the calculated delay value
    digitalWrite(targetPin,LOW); // write the buzzer pin low to pull back the diaphram
    delayMicroseconds(delayValue); // wait again or the calculated delay value
  }
  digitalWrite(LED_PISCA,LOW);
}

void sing(){
  int melody[] = {
  NOTE_E7, NOTE_E7, 0, NOTE_E7, 
  0, NOTE_C7, NOTE_E7, 0,
  };
 int size = sizeof(melody) / sizeof(int);
 for (int thisNote = 0; thisNote < size; thisNote++) {
   // to calculate the note duration, take one second
   // divided by the note type.
   //e.g. quarter note = 1000 / 4, eighth note = 1000/8, etc.
   int noteDuration = 1000/12;
   buzz(TONE_PIN, melody[thisNote],noteDuration);
   // to distinguish the notes, set a minimum time between them.
   // the note's duration + 30% seems to work well:
   int pauseBetweenNotes = noteDuration * 1.30;
   delay(pauseBetweenNotes);
   // stop the tone playing:
   buzz(TONE_PIN, 0,noteDuration);
  }
}
